// Logisim project guillemin_adder_test.circ as structural Verilog: 2 circuits, main circuit main
module main (
  input  in_1,
  output out_2
);

  wire add82_2_f3, add82_3_f3, add82_4_f3, button_1_out, button_2_out, button_3_out, button_4_out,
       button_5_out, button_6_out, button_7_out, button_8_out, button_9_out, button_10_out, button_11_out,
       button_12_out, button_13_out, button_14_out, button_15_out, button_16_out, button_17_out,
       decoder_1_out0, decoder_1_out1, decoder_1_out2, decoder_1_out3, decoder_1_out4, decoder_1_out5,
       decoder_1_out6, decoder_1_out7, register_1_q, register_6_q, register_11_q;
  wire [2:0] add82_1_f0, add82_2_f0, add82_3_f0, add82_4_f0, counter_1_q, counter_2_q, counter_3_q,
       counter_4_q, counter_5_q, counter_6_q, counter_7_q, counter_8_q, counter_9_q, counter_10_q,
       counter_11_q, demultiplexer_1_out0, demultiplexer_1_out1, demultiplexer_1_out2, demultiplexer_1_out3,
       demultiplexer_1_out4, demultiplexer_1_out5, demultiplexer_1_out6, demultiplexer_1_out7, ram_1_data,
       register_3_q, register_4_q, register_5_q, register_7_q, register_8_q, register_9_q, register_10_q;
  wire [3:0] bit_extender_1_out;

  Counter #(.width(3), .max('h7)) counter_1 (.Q(counter_1_q), .clk(button_1_out));  // open: load, D, count, carry, clr
  Button button_1 (.out(button_1_out));
  Counter #(.width(3), .max('h7)) counter_2 (.Q(counter_2_q), .clk(button_2_out));  // open: load, D, count, carry, clr
  Button button_2 (.out(button_2_out));
  Counter #(.width(3), .max('h7)) counter_3 (.Q(counter_3_q), .clk(button_3_out));  // open: load, D, count, carry, clr
  Button button_3 (.out(button_3_out));
  add82 add82_1 (
    .c(in_1), .a2(counter_1_q[2]), .a1(counter_1_q[1]), .a0(counter_1_q[0]), .b2(counter_3_q[2]),
    .b1(counter_3_q[1]), .in_7(counter_3_q[0]), .f0(add82_1_f0[0]), .f1(add82_1_f0[1]), .f2(add82_1_f0[2]),
    .f3(out_2));
  Counter #(.width(3), .max('h7)) counter_4 (.Q(counter_4_q), .clk(button_4_out));  // open: load, D, count, carry, clr
  Button button_4 (.out(button_4_out));
  add82 add82_2 (
    .c(register_1_q), .a2(counter_2_q[2]), .a1(counter_2_q[1]), .a0(counter_2_q[0]), .b2(counter_4_q[2]),
    .b1(counter_4_q[1]), .in_7(counter_4_q[0]), .f0(add82_2_f0[0]), .f1(add82_2_f0[1]), .f2(add82_2_f0[2]),
    .f3(add82_2_f3));
  Button button_5 (.out(button_5_out));
  Hex_Digit_Display hex_digit_display_1 (.value({1'b0, add82_1_f0}));  // open: dp
  Register #(.width(1)) register_1 (.D(add82_2_f3), .Q(register_1_q), .clk(button_5_out));  // open: en, clr
  Button button_6 (.out(button_6_out));
  Register #(.width(3)) register_2 (.D(register_3_q), .clk(button_13_out));  // open: en, Q, clr
  Register #(.width(3)) register_3 (.D(register_4_q), .Q(register_3_q), .clk(button_13_out));  // open: en, clr
  Counter #(.width(3), .max('h7)) counter_5 (.Q(counter_5_q), .clk(button_6_out));  // open: load, D, count, carry, clr
  Register #(.width(3)) register_4 (.D(register_5_q), .Q(register_4_q), .clk(button_13_out));  // open: en, clr
  Counter #(.width(3), .max('h7)) counter_6 (.Q(counter_6_q), .clk(button_7_out));  // open: load, D, count, carry, clr
  Button button_7 (.out(button_7_out));
  add82 add82_3 (
    .c(register_6_q), .a2(counter_5_q[2]), .a1(counter_5_q[1]), .a0(counter_5_q[0]), .b2(counter_6_q[2]),
    .b1(counter_6_q[1]), .in_7(counter_6_q[0]), .f0(add82_3_f0[0]), .f1(add82_3_f0[1]), .f2(add82_3_f0[2]),
    .f3(add82_3_f3));
  Button button_8 (.out(button_8_out));
  Register #(.width(3)) register_5 (.D(register_7_q), .Q(register_5_q), .clk(button_13_out));  // open: en, clr
  Button button_9 (.out(button_9_out));
  Register #(.width(1)) register_6 (
    .D(add82_3_f3), .Q(register_6_q), .clk(button_8_out), .clr(button_10_out));  // open: en
  Button button_10 (.out(button_10_out));
  Register #(.width(3)) register_7 (.D(register_8_q), .Q(register_7_q), .clk(button_13_out));  // open: en, clr
  Register #(.width(3)) register_8 (.D(register_9_q), .Q(register_8_q), .clk(button_13_out));  // open: en, clr
  Counter #(.width(3), .max('h7)) counter_7 (.Q(counter_7_q), .clk(button_9_out));  // open: load, D, count, carry, clr
  Register #(.width(3)) register_9 (.D(register_10_q), .Q(register_9_q), .clk(button_13_out));  // open: en, clr
  Button button_11 (.out(button_11_out));
  Button button_12 (.out(button_12_out));
  Register #(.width(3)) register_10 (.D(add82_2_f0), .Q(register_10_q), .clk(button_13_out));  // open: en, clr
  Button button_13 (.out(button_13_out));
  RAM #(.addrWidth(3), .dataWidth(3), .bus("separate")) ram_1 (
    .addr(counter_7_q), .din(add82_3_f0), .data(ram_1_data), .clk(button_11_out));  // open: str, sel, ld, clr
  assign bit_extender_1_out = {{1{1'b0}}, ram_1_data};  // Bit_Extender bit_extender_1
  Counter #(.width(3), .max('h7)) counter_8 (.Q(counter_8_q), .clk(button_12_out));  // open: load, D, count, carry, clr
  Hex_Digit_Display hex_digit_display_2 (.value(bit_extender_1_out));  // open: dp
  Counter #(.width(3), .max('h7)) counter_9 (.Q(counter_9_q), .clk(button_14_out));  // open: load, D, count, carry, clr
  Button button_14 (.out(button_14_out));
  add82 add82_4 (
    .c(register_11_q), .a2(counter_8_q[2]), .a1(counter_8_q[1]), .a0(counter_8_q[0]), .b2(counter_9_q[2]),
    .b1(counter_9_q[1]), .in_7(counter_9_q[0]), .f0(add82_4_f0[0]), .f1(add82_4_f0[1]), .f2(add82_4_f0[2]),
    .f3(add82_4_f3));
  Register #(.width(1)) register_11 (.D(add82_4_f3), .Q(register_11_q), .clk(button_15_out));  // open: en, clr
  Button button_15 (.out(button_15_out));
  Counter #(.width(3), .max('h7)) counter_10 (
    .load(1'b1), .Q(counter_10_q), .clk(button_16_out));  // open: D, count, carry, clr
  Button button_16 (.out(button_16_out));
  Button button_17 (.out(button_17_out));
  Demultiplexer #(.select(3), .width(3), .enable("false")) demultiplexer_1 (
    .out0(demultiplexer_1_out0), .out1(demultiplexer_1_out1), .out2(demultiplexer_1_out2),
    .out3(demultiplexer_1_out3), .out4(demultiplexer_1_out4), .out5(demultiplexer_1_out5),
    .out6(demultiplexer_1_out6), .out7(demultiplexer_1_out7), .in(add82_4_f0), .sel(counter_10_q));
  Register #(.width(3)) register_12 (.D(demultiplexer_1_out0), .clk(decoder_1_out0));  // open: en, Q, clr
  Decoder #(.select(3), .enable("false")) decoder_1 (
    .out0(decoder_1_out0), .out1(decoder_1_out1), .out2(decoder_1_out2), .out3(decoder_1_out3),
    .out4(decoder_1_out4), .out5(decoder_1_out5), .out6(decoder_1_out6), .out7(decoder_1_out7),
    .sel(counter_11_q));
  Counter #(.width(3), .max('h7)) counter_11 (
    .load(1'b1), .Q(counter_11_q), .clk(button_17_out));  // open: D, count, carry, clr
  Register #(.width(3)) register_13 (.D(demultiplexer_1_out1), .clk(decoder_1_out1));  // open: en, Q, clr
  Register #(.width(3)) register_14 (.D(demultiplexer_1_out2), .clk(decoder_1_out2));  // open: en, Q, clr
  Register #(.width(3)) register_15 (.D(demultiplexer_1_out3), .clk(decoder_1_out3));  // open: en, Q, clr
  Register #(.width(3)) register_16 (.D(demultiplexer_1_out5), .clk(decoder_1_out5));  // open: en, Q, clr
  Register #(.width(3)) register_17 (.D(demultiplexer_1_out4), .clk(decoder_1_out4));  // open: en, Q, clr
  Register #(.width(3)) register_18 (.D(demultiplexer_1_out7), .clk(decoder_1_out7));  // open: en, Q, clr
  Register #(.width(3)) register_19 (.D(demultiplexer_1_out6), .clk(decoder_1_out6));  // open: en, Q, clr

  // Notes on the sheet:
  //   TEST 1
  //   TEST 3
  //   TEST 2
  //   TEST 4
endmodule

module add82 (
  input  c,
  input  a2,
  input  a1,
  input  a0,
  input  b2,
  input  b1,
  input  in_7,
  output f0,
  output f1,
  output f2,
  output f3
);

  wire a0_prime, a1_prime, a2_prime, and00, and01, and02, and03, and10, and11, and12, and13, and14, and15,
       and16, and17, and18, and19, and20, and21, and22, and23, and24, and25, and26, and27, and28, and29,
       and30, and31, and32, and33, and34, and35, and36, and37, and38, and39, and110, and111, and210, and211,
       and212, and213, and214, and215, and216, and217, and218, and219, and220, and221, and222, and223,
       and224, and225, and226, and227, and310, and311, and312, and313, and314, b0_prime, b1_prime, b2_prime,
       c_prime;

  not not_1 (c_prime, c);
  not not_2 (a2_prime, a2);
  not not_3 (a1_prime, a1);
  and and_1 (and10, a1, a0_prime, b1_prime, b0_prime);
  and and_2 (and16, a1_prime, a0, b1_prime, in_7);
  and and_3 (and20, a2_prime, a1, b2_prime, b1);
  and and_4 (and25, a2, a0_prime, b2_prime, b1_prime, b0_prime);
  and and_5 (and210, c, a2_prime, a0, b2_prime, b1);
  and and_6 (and215, a2_prime, a1, a0, b2_prime, in_7);
  and and_7 (and220, c_prime, a2_prime, a1_prime, b2, b0_prime);
  and and_8 (and225, a2, a1, a0, b2, in_7);
  and and_9 (and30, a2, b2);
  and and_10 (and36, c, a0, b2, b1);
  and and_11 (and312, a0, b2, b1, in_7);
  not not_4 (a0_prime, a0);
  not not_5 (b2_prime, b2);
  and and_12 (and11, c_prime, a1, b1_prime, b0_prime);
  and and_13 (and17, c_prime, a1_prime, a0_prime, b1);
  and and_14 (and31, a2, a1, b1);
  and and_15 (and37, c, a1, b2, in_7);
  and and_16 (and313, a1, a0, b2, in_7);
  not not_6 (b0_prime, in_7);
  not not_7 (b1_prime, b1);
  and and_17 (and21, c_prime, a2, b2_prime, b1_prime, b0_prime);
  and and_18 (and26, c, a2_prime, a1, a0, b2_prime);
  and and_19 (and211, c, a2_prime, a1, b2_prime, in_7);
  and and_20 (and216, a2_prime, a0, b2_prime, b1, in_7);
  and and_21 (and221, a2, a1, b2, b1);
  and and_22 (and226, c, a2, b2, b1, in_7);
  and and_23 (and12, c, a1_prime, b1_prime, in_7);
  and and_24 (and18, c_prime, a1, a0_prime, b1_prime);
  and and_25 (and38, c, a2, a0, b1);
  and and_26 (and00, c, a0_prime, b0_prime);
  and and_27 (and22, a2_prime, a1_prime, a0_prime, b2, b0_prime);
  and and_28 (and27, a2, a1_prime, b2_prime, b1_prime);
  and and_29 (and32, a1, b2, b1);
  and and_30 (and314, a2, a1, a0, in_7);
  and and_31 (and13, a1_prime, a0_prime, b1, b0_prime);
  and and_32 (and19, c, a1, a0, b1);
  and and_33 (and212, c_prime, a2_prime, b2, b1_prime, b0_prime);
  and and_34 (and217, c_prime, a2, a0_prime, b2_prime, b1_prime);
  and and_35 (and222, c, a2, a1, b2, in_7);
  and and_36 (and227, a2, a0, b2, b1, in_7);
  and and_37 (and39, c, a2, a1, in_7);
  and and_38 (and01, c_prime, a0, b0_prime);
  and and_39 (and33, c, a2, a1, a0);
  and and_40 (and23, c, a2_prime, b2_prime, b1, in_7);
  and and_41 (and28, a2, a1_prime, a0_prime, b2_prime, b0_prime);
  and and_42 (and213, c_prime, a2, a1_prime, a0_prime, b2_prime);
  and and_43 (and218, c_prime, a2, a1_prime, b2_prime, b0_prime);
  and and_44 (and223, c, a2, a0, b2, b1);
  and and_45 (and02, c_prime, a0_prime, in_7);
  and and_46 (and14, c, a1_prime, a0, b1_prime);
  and and_47 (and110, a1, a0, b1, in_7);
  and and_48 (and34, c, a1, a0, b2);
  and and_49 (and310, c, a2, b1, in_7);
  and and_50 (and24, a2_prime, a1_prime, b2, b1_prime);
  and and_51 (and29, a2_prime, a0_prime, b2, b1_prime, b0_prime);
  and and_52 (and03, c, a0, in_7);
  and and_53 (and15, c_prime, a1_prime, b1, b0_prime);
  and and_54 (and111, c, a1, b1, in_7);
  and and_55 (and214, c_prime, a2_prime, a0_prime, b2, b1_prime);
  and and_56 (and219, c_prime, a2_prime, a1_prime, a0_prime, b2);
  and and_57 (and224, c, a2, a1, a0, b2);
  and and_58 (and35, c, b2, b1, in_7);
  and and_59 (and311, a2, a0, b1, in_7);
  or or_1 (f0, and00, and01, and02, and03);
  or or_2 (f1, and10, and11, and12, and13, and14, and15, and16, and17, and18, and19, and110, and111);
  or or_3 (f3, and30, and31, and32, and33, and34, and35, and36, and37, and38, and39, and310, and311, and312, and313, and314);
  or or_4 (f2, and20, and21, and22, and23, and24, and25, and26, and27, and28, and29, and210, and211, and212, and213, and214, and215, and216, and217, and218, and219, and220, and221, and222, and223, and224, and225, and226, and227);

  // Other names for the same wires on the sheet: b0 = in_7
endmodule
